# Fritzing sketch Model - Fritzing (saved by Fritzing 0.9.10b)
breadboards: 1

parts:
  Part1 = Arduino Mega 2560 (Rev3)
  Part2 = Arduino Board Ethernet  # not connected
  DHT1 = DHT22 Humidity and Temperature Sensor
  X1 = USB Connectors [package=usb-a-s-nosilk]
  X2 = USB Connectors [package=usb-a-s-nosilk]
  R1 = Resistor [tolerance=±5% power=0.25 resistance=10k package=THT]
  R2 = Resistor [tolerance=±5% power=0.25 resistance=10k package=THT]
  LED4 = smd LED [color="Red (633nm)" current=0A package="0805 [SMD]"]
  J1 = Piezo Speaker
  LED7 = LED - 3mm [color="Blue (470nm)" current=0.030 package="3 mm [THT]"]
  LED8 = LED - 3mm [color="Orange (620nm)" current=0.030 package="3 mm [THT]"]
  LED9 = LED - 3mm [color="Red (633nm)" current=0.030 package="3 mm [THT]"]
  S1 = Round Pushbutton

nets:
  N1: Part1.A8, X2.VBUS, R2.Pin_0
  N2: Part1.A9, X1.VBUS, R1.Pin_0
  N3: Part1.D28, DHT1.DATA
  N4: Part1.D29, LED7.anode
  N5: Part1.D30, LED8.anode
  N6: Part1.D31, LED9.anode
  N7: Part1.D32, LED4.anode
  N8: Part1.D33, J1.pin2
  N9: Part1.D34, S1.leg1
  GND: DHT1.GND, X1.GND, X2.GND, R1.Pin_1, R2.Pin_1, LED4.cathode, J1.pin1, LED7.cathode, LED8.cathode, LED9.cathode, S1.leg0

notes:
  Main Power
  Arduino MEGA + Ethernet Shield
  Backup Power
  Ceiling Light
